# Fritzing sketch cat-catcher (saved by Fritzing 0.9.3b)
breadboards: 1

parts:
  Raspberry_Pi1 = Raspberry Pi B+  # not connected
  Part1 = Adafruit 16-Channel PWM + Servo HAT [part_number="Adafruit #2327"]
  HC-SR04_Sensor_1 = HC-SR04 Ultrasonic Distance Sensor
  R1 = Resistor [tolerance=±5% resistance=1k package=THT]
  R2 = Resistor [tolerance=±5% resistance=2.2k package=THT]
  J1 = Basic Servo
  J2 = Basic Servo

nets:
  N1: Part1.GPIO23, HC-SR04_Sensor_1.TRIG
  N2: Part1.GPIO24, R1.Pin_1, R2.Pin_0
  N3: Part1.#1, J2.pulse
  VCC: Part1.+5V, J1.vcc, J2.vcc
  GND: Part1.GND, HC-SR04_Sensor_1.GND, R2.Pin_1, J1.gnd, J2.gnd
  N4: Part1.#0, J1.pulse
  N5: Part1.5.0V, HC-SR04_Sensor_1.VCC
  N6: HC-SR04_Sensor_1.ECHO, R1.Pin_0

notes:
  Ultrasonic
  Trigger Pin: 23
  Echo Pin: 24

custom parts:
  Adafruit 16-Channel PWM + Servo HAT: The Raspberry Pi is a wonderful little computer, but one thing it isn't very good at is controlling DC Servo Motors - these motors need very specific and repetitive timing pulses to set the position. Instead of asking the Pi Linux kernel to send these signals, pop on this handy HAT! It adds the capability to control 16 Servos with perfect timing. It can also do PWM up to 1.6 KHz with 12 bit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
